// Logisim project CircuitDiagram.circ as structural Verilog: 2 circuits, main circuit main
module main (
);

  InstructionManage instructionmanage_1 ();  // open: iB1, iB2, iB3, iB4, iB5, iB6, iB7, iB8, LOAD
  Clock clock_1 ();  // open: out
  ROM rom_1 ();  // open: addr, data
  ROM rom_2 ();  // open: addr, data
  ROM rom_3 ();  // open: addr, data

  // Notes on the sheet:
  //   CLOCK
  //   OPCODE
  //   OPERAND 1
  //   OPERAND 2
endmodule

module InstructionManage (
  input  iB1,
  input  iB2,
  input  iB3,
  input  iB4,
  input  iB5,
  input  iB6,
  input  iB7,
  input  iB8,
  output LOAD
);

  wire and_1_out, and_2_out, and_3_out, and_4_out, and_5_out, and_6_out, not_1_out, not_2_out, not_3_out,
       not_4_out, not_5_out, not_6_out, not_7_out, not_8_out;

  not not_1 (not_1_out, iB1);
  not not_2 (not_2_out, iB2);
  not not_3 (not_3_out, iB3);
  not not_4 (not_4_out, iB4);
  not not_5 (not_5_out, iB5);
  not not_6 (not_6_out, iB6);
  not not_7 (not_7_out, iB7);
  not not_8 (not_8_out, iB8);
  and and_1 (and_1_out, not_1_out, not_2_out);
  and and_2 (and_2_out, not_3_out, not_4_out);
  and and_3 (and_3_out, not_5_out, not_6_out);
  and and_4 (and_4_out, not_7_out, not_8_out);
  and and_5 (and_5_out, and_1_out, and_2_out);
  and and_6 (and_6_out, and_3_out, and_4_out);
  and and_7 (LOAD, and_5_out, and_6_out);

  // Notes on the sheet:
  //   INSTRUCTION DECONSTRUCTOR
  //   iB Refers To Instruction Bit
endmodule
